// Logisim project subleq.circ as structural Verilog: 1 circuit, main circuit main
module main (
);

  wire and_1_out, bit_extender_1_out, CLK_out, demultiplexer_1_out0, demultiplexer_1_out1,
       demultiplexer_1_out2, demultiplexer_1_out3, not_1_out, not_2_out, or_1_out, or_2_out, or_3_out;
  wire [1:0] Step_q;
  wire [7:0] bitselector_1_out, C_q, controlled_buffer_1_out, controlled_buffer_2_out, INS_q, INS_q_2,
       INS_q_3, PC_q;
  wire [23:0] A_q, B_q, ram_1_data, subtractor_1_out;

  assign controlled_buffer_1_out = or_3_out ? C_q : 8'bz;  // Controlled_Buffer controlled_buffer_1
  Counter #(.ongoal("stay"), .trigger("falling")) PC (
    .load(and_1_out), .D(controlled_buffer_1_out), .count(not_1_out), .Q(PC_q), .clk(demultiplexer_1_out3));  // open: carry, clr
  not not_1 (not_1_out, and_1_out);
  and and_1 (and_1_out, or_3_out, demultiplexer_1_out3);
  assign controlled_buffer_2_out = demultiplexer_1_out0 ? PC_q : 8'bz;  // Controlled_Buffer controlled_buffer_2
  assign controlled_buffer_2_out = demultiplexer_1_out1 ? INS_q_3 : 8'bz;  // Controlled_Buffer controlled_buffer_3
  assign controlled_buffer_2_out = or_1_out ? INS_q_2 : 8'bz;  // Controlled_Buffer controlled_buffer_4
  or or_1 (or_1_out, demultiplexer_1_out3, demultiplexer_1_out2);
  Clock CLK (.out(CLK_out));
  RAM #(.dataWidth(24), .bus("separate")) ram_1 (
    .addr(controlled_buffer_2_out), .din(subtractor_1_out), .data(ram_1_data), .str(demultiplexer_1_out3),
    .clk(CLK_out), .ld(or_2_out));  // open: sel, clr
  or or_2 (or_2_out, demultiplexer_1_out2, demultiplexer_1_out1, demultiplexer_1_out0);
  Register #(.width(24)) INS (
    .D(ram_1_data), .en(demultiplexer_1_out0), .Q({INS_q_3, INS_q_2, INS_q}), .clk(CLK_out));  // open: clr
  BitSelector #(.width(24), .group(8)) bitselector_1 (.in(ram_1_data), .out(bitselector_1_out), .sel(2'b00));
  Register #(.width(24)) B (.D(ram_1_data), .en(demultiplexer_1_out2), .Q(B_q), .clk(CLK_out));  // open: clr
  Register #(.width(24)) A (.D(ram_1_data), .en(demultiplexer_1_out1), .Q(A_q), .clk(CLK_out));  // open: clr
  or or_3 (or_3_out, subtractor_1_out[23], ~bit_extender_1_out);  // OR_Gate
  Register C (.D(bitselector_1_out), .en(demultiplexer_1_out0), .Q(C_q), .clk(CLK_out));  // open: clr
  Subtractor #(.width(24)) subtractor_1 (.a(B_q), .b(A_q), .out(subtractor_1_out));  // open: bin, bout
  Demultiplexer #(.select(2)) demultiplexer_1 (
    .out0(demultiplexer_1_out0), .out1(demultiplexer_1_out1), .out2(demultiplexer_1_out2),
    .out3(demultiplexer_1_out3), .in(not_2_out), .sel(Step_q));  // open: en
  not not_2 (not_2_out, CLK_out);
  Counter #(.width(2), .max('h3), .trigger("falling")) Step (
    .Q(Step_q), .clk(CLK_out));  // open: load, D, count, carry, clr
  Bit_Extender #(.in_width(24), .out_width(1)) bit_extender_1 (.in(subtractor_1_out), .out(bit_extender_1_out));
endmodule
